// Logisim project mainALU.circ as structural Verilog: 1 circuit, main circuit main
module main (
  input  A7,
  input  A6,
  input  A5,
  input  A4,
  input  A3,
  input  A2,
  input  A1,
  input  A0,
  input  B7,
  input  B6,
  input  B5,
  input  B4,
  input  B3,
  input  B2,
  input  B1,
  input  B0,
  input  in_17,
  input  in_18,
  input  in_19,
  output R7,
  output R6,
  output R5,
  output R4,
  output R3,
  output R2,
  output R1,
  output R0,
  output out_28
);

  wire minus_OVERFLOW, OVERFLOW, plus_OVERFLOW;
  wire [7:0] A, B, demultiplexer_1_out3, demultiplexer_1_out4, demultiplexer_2_out3, demultiplexer_2_out4,
       minus_A, minus_B, minus_R, nA, nB, nR, plus_A, plus_B, plus_R, R, R_t;

  // soma SOMA: pin names not known; wires that end beside it: plus_A[7], plus_A[6], plus_R[7], plus_A[5], plus_R[6], plus_A[4], plus_R[5], plus_A[3], plus_R[4], plus_A[2], plus_R[3], plus_A[1], plus_R[2], plus_A[0], plus_R[1], plus_B[7], plus_R[0], plus_B[6], plus_B[5], plus_B[4], plus_B[3], plus_B[2], plus_B[1], plus_B[0], plus_OVERFLOW
  subtracVfinale_main SUBTRACAO (
    .x(minus_A[7]), .y(minus_B[7]), .out(minus_R[7]), .in_2(minus_A[6]), .in_10(minus_B[6]),
    .out_19(minus_R[6]), .in_3(minus_A[5]), .in_11(minus_B[5]), .out_20(minus_R[5]), .in_4(minus_A[4]),
    .in_12(minus_B[4]), .out_21(minus_R[4]), .in_5(minus_A[3]), .in_13(minus_B[3]), .out_22(minus_R[3]),
    .in_6(minus_A[2]), .in_14(minus_B[2]), .out_23(minus_R[2]), .in_7(minus_A[1]), .in_15(minus_B[1]),
    .out_24(minus_R[1]), .in_8(minus_A[0]), .in_16(minus_B[0]), .out_25(minus_R[0]), .overflow(minus_OVERFLOW));
  Demultiplexer #(.select(3), .width(8), .enable("false")) demultiplexer_1 (
    .out0(plus_A), .out1(minus_A), .out2(A), .out3(demultiplexer_1_out3), .out4(demultiplexer_1_out4),
    .in({A0, A1, A2, A3, A4, A5, A6, A7}), .sel({in_17, in_18, in_19}));  // open: out5, out6, out7
  Demultiplexer #(.select(3), .width(8), .enable("false")) demultiplexer_2 (
    .out0(plus_B), .out1(minus_B), .out2(B), .out3(demultiplexer_2_out3), .out4(demultiplexer_2_out4),
    .in({B0, B1, B2, B3, B4, B5, B6, B7}), .sel({in_17, in_18, in_19}));  // open: out5, out6, out7
  assign nA = demultiplexer_1_out3 | demultiplexer_1_out4;  // OR_Gate or_1, 8 bits wide
  assign nB = demultiplexer_2_out3 | demultiplexer_2_out4;  // OR_Gate or_2, 8 bits wide
  divider_main DIVISAO_RESTO (
    .in_1(nA[7]), .in_2(nA[6]), .in_3(nA[5]), .in_4(nA[4]), .in_5(nA[3]), .in_6(nA[2]), .in_7(nA[1]),
    .in_8(nA[0]), .in_9(nB[7]), .in_10(nB[6]), .in_11(nB[5]), .in_12(nB[4]), .in_13(nB[3]), .in_14(nB[2]),
    .in_15(nB[1]), .in_16(nB[0]), .out_17(nR[7]), .out_18(nR[6]), .out_19(nR[5]), .out_20(nR[4]),
    .out_21(nR[3]), .out_22(nR[2]), .out_23(nR[1]), .out_24(nR[0]), .out_25(R[7]), .out_26(R[6]),
    .out_27(R[5]), .out_28(R[4]), .out_29(R[3]), .out_30(R[2]), .out_31(R[1]), .out_32(R[0]));
  or or_3 (out_28, plus_OVERFLOW, minus_OVERFLOW, OVERFLOW);
  Multiplexer #(.select(3), .width(8), .enable("false")) multiplexer_1 (
    .in0(plus_R), .in1(minus_R), .in2(R_t), .in3(nR), .in4(R), .out({R0, R1, R2, R3, R4, R5, R6, R7}),
    .sel({in_17, in_18, in_19}));  // open: in5, in6, in7
  multiplier_main MULTIPLICACAO (
    .out_17(OVERFLOW), .in_1(A[7]), .in_9(B[7]), .out_18(R_t[7]), .in_2(A[6]), .in_10(B[6]), .out_19(R_t[6]),
    .in_3(A[5]), .in_4(A[4]), .in_11(B[5]), .out_20(R_t[5]), .in_5(A[3]), .in_12(B[4]), .out_21(R_t[4]),
    .in_6(A[2]), .in_7(A[1]), .in_13(B[3]), .out_22(R_t[3]), .in_8(A[0]), .in_14(B[2]), .out_23(R_t[2]),
    .in_15(B[1]), .out_24(R_t[1]), .in_16(B[0]), .out_25(R_t[0]));

  // Other names for the same wires on the sheet: A_t[7:0] = {A0, A1, A2, A3, A4, A5, A6, A7};
  //   B_t[7:0] = {B0, B1, B2, B3, B4, B5, B6, B7}; OVERFLOW_t = out_28; R_t_t[7:0] = {R0, R1, R2, R3, R4, R5, R6, R7};
  //   SEL[2:0] = {in_17, in_18, in_19}
endmodule
