// Logisim project Controlador.circ as structural Verilog: 1 circuit, main circuit main
// 8
module main (
);

  wire and_2_out, clock_1_out, JMP, LDA, not_1_out, not_2_out, not_3_out, not_4_out, PC_plus_plus, Pega_PC,
       refresh, reset, STA, stop;
  wire [0:0] and_1_out;
  wire [1:0] counter_1_q;
  wire [7:0] AB, \Endereço , \Instrução , PC;
  wire [15:0] Acc, setAcc, setIR, transistor_1_out, Valor;

  Clock clock_1 (.out(clock_1_out));
  Register #(.width(16)) IR (.D(setIR), .en(Pega_PC), .Q({\Instrução , AB}), .clk(clock_1_out), .clr(1'b0));
  not not_1 (not_1_out, Pega_PC);
  Multiplexer #(.select(2), .width(8), .enable("false")) multiplexer_1 (
    .in0(PC), .in1(AB), .in2(AB), .out(\Endereço ), .sel({STA, and_1_out[0]}));  // open: in3
  and and_1 (and_1_out[0], LDA, not_1_out);
  Demultiplexer #(.width(16), .enable("false")) demultiplexer_1 (
    .out0(setIR), .out1(setAcc), .in(Valor), .sel(and_1_out[0]));
  Button button_1 (.out(reset));
  Register #(.width(16)) Acumulador (.D(setAcc), .en(LDA), .Q(Acc), .clk(clock_1_out), .clr(1'b0));
  Counter #(.width(2), .max('h2)) counter_1 (
    .Q(counter_1_q), .clk(and_2_out), .clr(reset));  // open: load, D, count, carry
  and and_2 (and_2_out, clock_1_out, ~stop);  // AND_Gate
  Demultiplexer #(.select(2), .enable("false")) demultiplexer_2 (
    .out0(Pega_PC), .out1(refresh), .out2(PC_plus_plus), .in(1'b1), .sel(counter_1_q));  // open: out3
  not not_2 (not_2_out, refresh);
  not not_3 (not_3_out, STA);
  IF_main main_1 (
    .out_3(LDA), .out_7(JMP), .STA(STA), .out_5(stop), .in_1(\Instrução ), .in_2(refresh));  // open: out_6
  Transistor #(.\type ("n"), .width(16)) transistor_1 (.in(Acc), .out(transistor_1_out), .gate(STA));
  RAM #(.dataWidth(16)) ram_1 (
    .addr(\Endereço ), .data(transistor_1_out), .sel(1'b1), .clk(not_2_out), .ld(not_3_out), .clr(1'b0));
  not not_4 (not_4_out, STA);
  Transistor #(.\type ("n"), .width(16)) transistor_2 (.in(transistor_1_out), .out(Valor), .gate(not_4_out));
  // Probe on AB
  PC_main main_2 (.in_1(PC_plus_plus), .in_2(reset), .out_5(PC), .in_4(AB), .in_3(JMP));
endmodule
