// Logisim project IF.circ as structural Verilog: 1 circuit, main circuit main
module main (
  input  [7:0] in_1,
  output out_2,
  output out_3,
  output out_4,
  output out_5,
  output out_6
);

  and and_1 (out_4, ~in_1[0], in_1[1], ~in_1[2], ~in_1[3], in_1[4], in_1[5], ~in_1[6], ~in_1[7]);  // AND_Gate
  and and_2 (out_2, in_1[0], in_1[1], ~in_1[2], in_1[3], ~in_1[4], ~in_1[5], ~in_1[6], ~in_1[7]);  // AND_Gate
  and and_3 (out_3, ~in_1[0], ~in_1[1], in_1[2], in_1[3], ~in_1[4], ~in_1[5], ~in_1[6], ~in_1[7]);  // AND_Gate
  and and_4 (out_5, in_1[0], ~in_1[1], ~in_1[2], ~in_1[3], in_1[4], in_1[5], ~in_1[6], ~in_1[7]);  // AND_Gate
  and and_5 (out_6, ~in_1[0], in_1[1], in_1[2], ~in_1[3], ~in_1[4], ~in_1[5], in_1[6], ~in_1[7]);  // AND_Gate

  // Other names for the same wires on the sheet: _0 = in_1[0]; _1 = in_1[1]; _2 = in_1[2]; _3 = in_1[3]; _4 = in_1[4];
  //   _5 = in_1[5]; _6 = in_1[6]; _7 = in_1[7]

  // Notes on the sheet:
  //   Load
  //   NOP
  //   STA
  //   JMP
  //   STP
endmodule
