// Logisim project PC.circ as structural Verilog: 1 circuit, main circuit main
module main (
  input  in_1,
  input  in_2,
  input  [7:0] in_3,
  output [7:0] out_4
);

  wire j_k_ff_1_qn, j_k_ff_2_qn, j_k_ff_3_qn, j_k_ff_4_qn, j_k_ff_5_qn, j_k_ff_6_qn, j_k_ff_7_qn;

  J_K_Flip_Flop j_k_ff_1 (
    .J(1'b1), .clk(in_1), .K(1'b1), .Q(out_4[0]), .Qn(j_k_ff_1_qn), .preset(in_3[0]), .en(1'b1), .reset(in_2));
  J_K_Flip_Flop j_k_ff_2 (
    .J(1'b1), .clk(j_k_ff_1_qn), .K(1'b1), .Q(out_4[1]), .Qn(j_k_ff_2_qn), .preset(in_3[1]), .en(1'b1),
    .reset(in_2));
  J_K_Flip_Flop j_k_ff_3 (
    .J(1'b1), .clk(j_k_ff_2_qn), .K(1'b1), .Q(out_4[2]), .Qn(j_k_ff_3_qn), .preset(in_3[2]), .en(1'b1),
    .reset(in_2));
  J_K_Flip_Flop j_k_ff_4 (
    .J(1'b1), .clk(j_k_ff_5_qn), .K(1'b1), .Q(out_4[4]), .Qn(j_k_ff_4_qn), .preset(in_3[4]), .en(1'b1),
    .reset(in_2));
  J_K_Flip_Flop j_k_ff_5 (
    .J(1'b1), .clk(j_k_ff_3_qn), .K(1'b1), .Q(out_4[3]), .Qn(j_k_ff_5_qn), .preset(in_3[3]), .en(1'b1),
    .reset(in_2));
  J_K_Flip_Flop j_k_ff_6 (
    .J(1'b1), .clk(j_k_ff_4_qn), .K(1'b1), .Q(out_4[5]), .Qn(j_k_ff_6_qn), .preset(in_3[5]), .en(1'b1),
    .reset(in_2));
  J_K_Flip_Flop j_k_ff_7 (
    .J(1'b1), .clk(j_k_ff_6_qn), .K(1'b1), .Q(out_4[6]), .Qn(j_k_ff_7_qn), .preset(in_3[6]), .en(1'b1),
    .reset(in_2));
  J_K_Flip_Flop j_k_ff_8 (
    .J(1'b1), .clk(j_k_ff_7_qn), .K(1'b1), .Q(out_4[7]), .preset(in_3[7]), .en(1'b1), .reset(in_2));  // open: Qn
endmodule
