// Logisim project subtracV2.circ as structural Verilog: 1 circuit, main circuit main
module main (
  input  x,
  input  in_2,
  input  in_3,
  input  in_4,
  input  in_5,
  input  in_6,
  input  in_7,
  input  in_8,
  input  y,
  input  in_10,
  input  in_11,
  input  in_12,
  input  in_13,
  input  in_14,
  input  in_15,
  input  in_16,
  input  borrow_in,
  output overflow,
  output out_19,
  output out_20,
  output out_21,
  output out_22,
  output out_23,
  output out_24,
  output out_25,
  output out_26
);

  wire and_1_out, and_2_out, and_3_out, and_4_out, and_5_out, and_6_out, and_7_out, and_8_out, and_9_out,
       and_10_out, and_11_out, and_12_out, and_13_out, and_14_out, and_15_out, and_16_out, not_1_out,
       not_2_out, not_3_out, not_4_out, not_5_out, not_6_out, not_7_out, not_8_out, or_1_out, or_2_out,
       or_3_out, or_4_out, or_5_out, or_6_out, or_7_out, xor_1_out, xor_3_out, xor_5_out, xor_8_out,
       xor_9_out, xor_11_out, xor_13_out, xor_16_out;

  not not_1 (not_1_out, x);
  xor xor_1 (xor_1_out, x, y);
  xor xor_2 (out_19, borrow_in, xor_1_out);
  and and_1 (and_1_out, not_1_out, borrow_in);
  and and_2 (and_2_out, y, borrow_in);
  or or_1 (or_1_out, and_1_out, and_2_out);
  xor xor_3 (xor_3_out, in_2, in_10);
  xor xor_4 (out_20, or_1_out, xor_3_out);
  not not_2 (not_2_out, in_2);
  and and_3 (and_3_out, not_2_out, or_1_out);
  and and_4 (and_4_out, in_10, or_1_out);
  or or_2 (or_2_out, and_3_out, and_4_out);
  xor xor_5 (xor_5_out, in_3, in_11);
  xor xor_6 (out_21, or_2_out, xor_5_out);
  not not_3 (not_3_out, in_3);
  and and_5 (and_5_out, not_3_out, or_2_out);
  and and_6 (and_6_out, in_11, or_2_out);
  or or_3 (or_3_out, and_5_out, and_6_out);
  xor xor_7 (out_22, or_3_out, xor_8_out);
  not not_4 (not_4_out, in_4);
  xor xor_8 (xor_8_out, in_4, in_12);
  and and_7 (and_7_out, not_4_out, or_3_out);
  and and_8 (and_8_out, in_12, or_3_out);
  or or_4 (or_4_out, and_7_out, and_8_out);
  not not_5 (not_5_out, in_5);
  xor xor_9 (xor_9_out, in_5, in_13);
  xor xor_10 (out_23, or_4_out, xor_9_out);
  and and_9 (and_9_out, not_5_out, or_4_out);
  and and_10 (and_10_out, in_13, or_4_out);
  or or_5 (or_5_out, and_9_out, and_10_out);
  xor xor_11 (xor_11_out, in_6, in_14);
  xor xor_12 (out_24, or_5_out, xor_11_out);
  not not_6 (not_6_out, in_6);
  and and_11 (and_11_out, not_6_out, or_5_out);
  and and_12 (and_12_out, in_14, or_5_out);
  or or_6 (or_6_out, and_11_out, and_12_out);
  xor xor_13 (xor_13_out, in_7, in_15);
  xor xor_14 (out_25, or_6_out, xor_13_out);
  not not_7 (not_7_out, in_7);
  and and_13 (and_13_out, not_7_out, or_6_out);
  and and_14 (and_14_out, in_15, or_6_out);
  or or_7 (or_7_out, and_13_out, and_14_out);
  xor xor_15 (out_26, or_7_out, xor_16_out);
  not not_8 (not_8_out, in_8);
  xor xor_16 (xor_16_out, in_8, in_16);
  and and_15 (and_15_out, not_8_out, or_7_out);
  and and_16 (and_16_out, in_16, or_7_out);
  or or_8 (overflow, and_15_out, and_16_out);

  // Notes on the sheet:
  //   out
endmodule
